// Logisim project aluViva.circ as structural Verilog: 1 circuit, main circuit main
module main (
  input  Cin,
  input  A,
  input  B,
  input  in_4,
  input  isAdd,
  input  isSub,
  input  isMul,
  input  shift,
  output cout,
  output out_10
);

  wire adder_1_out, multiplier_1_out, shifter_1_out, subtractor_1_out;
  wire [1:0] priority_encoder_1_out;

  Adder #(.width(1)) adder_1 (.a(A), .b(B), .out(adder_1_out), .cin(Cin), .cout(cout));
  Subtractor #(.width(1)) subtractor_1 (.a(A), .b(B), .out(subtractor_1_out), .bin(Cin));  // open: bout
  Multiplier #(.width(1)) multiplier_1 (.a(A), .b(B), .out(multiplier_1_out), .cin(Cin));  // open: cout
  Shifter #(.width(1)) shifter_1 (.in(A), .\dist (B), .out(shifter_1_out));
  Multiplexer #(.select(2)) multiplexer_1 (
    .in0(adder_1_out), .in1(subtractor_1_out), .in2(multiplier_1_out), .in3(shifter_1_out), .out(out_10),
    .sel(priority_encoder_1_out), .en(in_4));
  Priority_Encoder #(.select(2)) priority_encoder_1 (
    .in0(isAdd), .in1(isSub), .in2(isMul), .in3(shift), .out(priority_encoder_1_out));
endmodule
